# Fritzing sketch DistanceSensor (saved by Fritzing 0.9.1b)

parts:
  Componente1 = SRF05 Ultrasonic Rangefinder
  Componente2 = Arduino Uno (Rev3)

nets:
  VCC: Componente1.VCC, Componente2.5V
  N1: Componente1.Trig, Componente2.D7
  N2: Componente1.Echo, Componente2.D8
  GND: Componente1.GND, Componente2.GND
